# Fritzing sketch JoystickConArduino (saved by Fritzing 0.9.3b)

parts:
  Part1 = Thumb Joystick
  Part2 = Arduino Uno (Rev3)

nets:
  GND: Part1.GND, Part2.GND
  N1: Part1.SEL, Part2.D2
  N2: Part1.HORZ, Part2.A0
  N3: Part1.VERT, Part2.A1
  VCC: Part1.VCC, Part2.5V
